// Logisim project 4bitparity.circ as structural Verilog: 5 circuits, main circuit main
module main (
  input  Halt_Enable
);

  wire and_2_out, CLK, Correct, Done_Testing, Halt, Input, not_1_out, not_2_out, not_3_out, Solution,
       YourAnswer;
  wire [6:0] counter_1_q, TestNumber;

  not not_1 (not_1_out, Correct);
  Clock clock_1 (.out(CLK));
  and and_1 (Halt, Halt_Enable, not_1_out);
  Inputs inputs_1 (.Halt(Halt), .CLK(CLK), .Input(Input), .TestNumber(TestNumber), .Done_Testing(Done_Testing));
  _4BitEvenParity u_4bitevenparity_1 (.Input(Input), .CLK(CLK), .Is_Even(YourAnswer));
  // Probe on Input
  // Probe on YourAnswer
  // Probe on Solution
  // Probe on Correct
  not not_2 (not_2_out, Halt);
  and and_2 (and_2_out, Correct, not_2_out, not_3_out);
  not not_3 (not_3_out, Done_Testing);
  Checker checker_1 (.Your_Answer(YourAnswer), .TestNumber(TestNumber), .Correct(Correct), .Solution(Solution));
  Counter #(.width(7), .max('h41), .ongoal("stay")) counter_1 (
    .count(and_2_out), .Q(counter_1_q), .clk(CLK));  // open: load, D, carry, clr
  // Probe on counter_1_q

  // Notes on the sheet:
  //   Kevin Trujillo
  //   Max 65
endmodule

module _4BitEvenParity (
  input  Input,
  input  CLK,
  output Is_Even
);

  wire d_ff_1_q, d_ff_2_q, d_ff_3_q, d_ff_4_q, evenparity_1_b0, evenparity_1_b1, evenparity_1_b2,
       evenparity_1_b3;

  EvenParity evenparity_1 (
    .a0(d_ff_1_q), .a1(d_ff_2_q), .a2(d_ff_3_q), .a3(d_ff_4_q), .in(Input), .b0(evenparity_1_b0),
    .b1(evenparity_1_b1), .b2(evenparity_1_b2), .b3(evenparity_1_b3), .Out(Is_Even));
  D_Flip_Flop d_ff_1 (.clk(CLK), .D(evenparity_1_b0), .Q(d_ff_1_q));  // open: Qn, preset, en, reset
  D_Flip_Flop d_ff_2 (.clk(CLK), .D(evenparity_1_b1), .Q(d_ff_2_q));  // open: Qn, preset, en, reset
  D_Flip_Flop d_ff_3 (.clk(CLK), .D(evenparity_1_b2), .Q(d_ff_3_q));  // open: Qn, preset, en, reset
  D_Flip_Flop d_ff_4 (.clk(CLK), .D(evenparity_1_b3), .Q(d_ff_4_q));  // open: Qn, preset, en, reset
endmodule

module Inputs (
  input  Halt,
  input  CLK,
  output Input,
  output [6:0] TestNumber,
  output Done_Testing
);

  wire not_1_out;

  not not_1 (not_1_out, Halt);
  Counter #(.width(7), .max('h41), .ongoal("stay")) counter_1 (
    .count(not_1_out), .Q(TestNumber), .carry(Done_Testing), .clk(CLK));  // open: load, D, clr
  ROM #(.addrWidth(7), .dataWidth(1)) rom_1 (.addr(TestNumber), .data(Input));  // open: sel

  // Notes on the sheet:
  //   contents of rom_1 (hex, n*v repeats v):
  //   7*0 1 0 0 1 0 0 0 1 1 0 1 0 0 0 1 0 1 0 1 1 0 0 4*1 0 0 0 1 0 0 1 1 0 1 0 1 0 4*1 0 0 1 1 0 4*1 0
  //   4*1
endmodule

module Checker (
  input  Your_Answer,
  input  [6:0] TestNumber,
  output Correct,
  output Solution
);

  ROM #(.addrWidth(7), .dataWidth(1)) rom_1 (.addr(TestNumber), .data(Solution));  // open: sel
  Comparator #(.width(1)) comparator_1 (.a(Solution), .b(Your_Answer), .eq(Correct));  // open: gt, lt

  // Notes on the sheet:
  //   contents of rom_1 (hex, n*v repeats v):
  //   4*0 1 11*0 1 7*0 1 0 0 0 1 11*0 1 0 0 0 1 7*0 1 11*0 1
endmodule

module EvenParity (
  input  a0,
  input  a1,
  input  a2,
  input  a3,
  input  in,
  output b0,
  output b1,
  output b2,
  output b3,
  output Out
);

  wire and_2_out, and_3_out, and_4_out, and_5_out, and_6_out, and_7_out, and_8_out, and_9_out, and_10_out,
       and_11_out, and_12_out, and_13_out, and_14_out, and_15_out, and_16_out, and_17_out, and_18_out,
       and_19_out, and_20_out, not_1_out, not_2_out, not_3_out, not_4_out, not_5_out, not_6_out, not_7_out,
       not_8_out, not_9_out, not_10_out, not_11_out, not_12_out, not_13_out, not_14_out, not_15_out,
       not_16_out, not_17_out, not_18_out, not_19_out, not_20_out, not_21_out, not_22_out, not_23_out,
       not_24_out;

  and and_1 (Out, a0, ~a1, ~a2, a3);  // AND_Gate
  not not_1 (not_1_out, a0);
  not not_2 (not_2_out, in);
  not not_3 (not_3_out, a2);
  not not_4 (not_4_out, a3);
  not not_5 (not_5_out, a0);
  not not_6 (not_6_out, a1);
  not not_7 (not_7_out, a0);
  not not_8 (not_8_out, in);
  not not_9 (not_9_out, a1);
  not not_10 (not_10_out, a0);
  not not_11 (not_11_out, a3);
  not not_12 (not_12_out, a3);
  not not_13 (not_13_out, a1);
  not not_14 (not_14_out, a2);
  not not_15 (not_15_out, a3);
  not not_16 (not_16_out, in);
  not not_17 (not_17_out, a0);
  not not_18 (not_18_out, a1);
  not not_19 (not_19_out, in);
  not not_20 (not_20_out, in);
  not not_21 (not_21_out, in);
  not not_22 (not_22_out, a3);
  not not_23 (not_23_out, a2);
  not not_24 (not_24_out, a3);
  and and_2 (and_2_out, not_1_out, a3, in);
  and and_3 (and_3_out, a1, not_2_out);
  and and_4 (and_4_out, a1, a3);
  and and_5 (and_5_out, a0, not_3_out, not_4_out);
  and and_6 (and_6_out, not_5_out, not_6_out, in);
  and and_7 (and_7_out, not_7_out, a3, not_8_out);
  and and_8 (and_8_out, not_9_out, a3, in);
  and and_9 (and_9_out, a2, in);
  and and_10 (and_10_out, not_10_out, a1, not_11_out);
  and and_11 (and_11_out, a1, not_12_out, in);
  and and_12 (and_12_out, a1, a2);
  and and_13 (and_13_out, a0, not_13_out, not_14_out, not_15_out, not_16_out);
  and and_14 (and_14_out, a0, a1, a3, in);
  and and_15 (and_15_out, not_17_out, not_18_out, not_19_out);
  and and_16 (and_16_out, a3, not_20_out);
  and and_17 (and_17_out, a2, not_21_out);
  and and_18 (and_18_out, a1, not_22_out, in);
  and and_19 (and_19_out, a1, a2);
  and and_20 (and_20_out, a0, not_23_out, not_24_out, in);
  or or_1 (b0, and_2_out, and_3_out, and_4_out, and_5_out);
  or or_2 (b1, and_6_out, and_7_out, and_8_out, and_9_out, and_10_out, and_11_out, and_12_out);
  or or_3 (b2, and_13_out, and_14_out);
  or or_4 (b3, and_15_out, and_16_out, and_17_out, and_18_out, and_19_out, and_20_out);
endmodule
