// Logisim project updowncounter.circ as structural Verilog: 5 circuits, main circuit main
module main (
  input  Halt_Enable
);

  wire and_2_out, CLK, Correct, Count_Down, Count_Up, Done_Testing, Halt, not_1_out, not_2_out, not_3_out;
  wire [2:0] Solution, Your_Answer;
  wire [5:0] counter_1_q;

  not not_1 (not_1_out, Correct);
  Clock clock_1 (.out(CLK));
  and and_1 (Halt, Halt_Enable, not_1_out);
  Inputs inputs_1 (.Halt(Halt), .CLK(CLK), .Count_Up(Count_Up), .Count_Down(Count_Down), .Done_Testing(Done_Testing));
  // Probe on Count_Up
  // Probe on Count_Down
  // Probe on Your_Answer
  // Probe on Solution
  Up_Down_Counter up_down_counter_1 (
    .Count_Up(Count_Up), .Count_Down(Count_Down), .CLK(CLK), .Count(Your_Answer));  // open: y0, y1, y2
  not not_2 (not_2_out, Halt);
  not not_3 (not_3_out, Done_Testing);
  Counter #(.width(6), .max('h21), .ongoal("stay")) counter_1 (
    .count(and_2_out), .Q(counter_1_q), .clk(CLK));  // open: load, D, carry, clr
  and and_2 (and_2_out, Correct, not_2_out, not_3_out);
  Checker checker_1 (
    .Halt_Enable(Halt_Enable), .Count_Up(Count_Up), .Count_Donw(Count_Down), .Your_Answer(Your_Answer),
    .CLK(CLK), .Correct(Correct), .Solution(Solution));
  // Probe on counter_1_q

  // Notes on the sheet:
  //   Your Solution in Here
  //   Max of 33
endmodule

module Up_Down_Counter (
  input  Count_Up,
  input  Count_Down,
  input  CLK,
  output [2:0] Count,
  output y0,
  output y1,
  output y2
);

  wire and_1_out, and_2_out, and_3_out, and_4_out, and_5_out, and_6_out, and_7_out, and_8_out, and_9_out,
       and_10_out, and_11_out, and_12_out, and_13_out, and_14_out, and_15_out, and_16_out, and_17_out,
       not_1_out, not_2_out, not_3_out, not_4_out, not_5_out, not_6_out, not_7_out, not_8_out, not_9_out,
       not_10_out, not_11_out, not_12_out, not_13_out, not_14_out, not_15_out, not_16_out, not_17_out,
       not_18_out, not_19_out, not_20_out;

  not not_1 (not_1_out, Count_Down);
  not not_2 (not_2_out, Count_Down);
  not not_3 (not_3_out, Count[1]);
  not not_4 (not_4_out, Count_Down);
  not not_5 (not_5_out, Count[0]);
  not not_6 (not_6_out, Count_Down);
  not not_7 (not_7_out, Count_Up);
  not not_8 (not_8_out, Count[1]);
  not not_9 (not_9_out, Count[0]);
  not not_10 (not_10_out, Count_Up);
  not not_11 (not_11_out, Count_Down);
  not not_12 (not_12_out, Count[0]);
  not not_13 (not_13_out, Count_Down);
  not not_14 (not_14_out, Count_Up);
  not not_15 (not_15_out, Count_Down);
  and and_1 (and_1_out, Count[0], Count_Up, Count_Down);
  not not_16 (not_16_out, Count[0]);
  not not_17 (not_17_out, Count_Up);
  not not_18 (not_18_out, Count[0]);
  not not_19 (not_19_out, Count_Up);
  not not_20 (not_20_out, Count_Down);
  and and_2 (and_2_out, Count[1], Count[0], Count_Up, not_1_out);
  and and_3 (and_3_out, Count[2], not_2_out);
  and and_4 (and_4_out, Count[2], Count_Up);
  and and_5 (and_5_out, Count[2], Count[0]);
  and and_6 (and_6_out, Count[2], Count[1]);
  and and_7 (and_7_out, not_3_out, Count[0], Count_Up, not_4_out);
  and and_8 (and_8_out, Count[1], not_5_out, not_6_out);
  and and_9 (and_9_out, Count[1], Count_Up, Count_Down);
  and and_10 (and_10_out, Count[1], Count[0], not_7_out);
  and and_11 (and_11_out, Count[2], not_8_out, not_9_out, not_10_out, Count_Down);
  and and_12 (and_12_out, Count[2], Count[1], not_11_out);
  and and_13 (and_13_out, not_12_out, Count_Up, not_13_out);
  and and_14 (and_14_out, Count[0], not_14_out, not_15_out);
  and and_15 (and_15_out, Count[1], not_16_out, not_17_out, Count_Down);
  and and_16 (and_16_out, Count[2], not_18_out, not_19_out, Count_Down);
  and and_17 (and_17_out, Count[2], Count[1], Count[0], not_20_out);
  or or_1 (y0, and_2_out, and_3_out, and_4_out, and_5_out, and_6_out);
  or or_2 (y1, and_7_out, and_8_out, and_9_out, and_10_out, and_11_out, and_12_out);
  or or_3 (y2, and_13_out, and_14_out, and_1_out, and_15_out, and_16_out, and_17_out);
  D_Flip_Flop d_ff_1 (.clk(CLK), .D(y0), .Q(Count[2]));  // open: Qn, preset, en, reset
  D_Flip_Flop d_ff_2 (.clk(CLK), .D(y2), .Q(Count[0]));  // open: Qn, preset, en, reset
  D_Flip_Flop d_ff_3 (.clk(CLK), .D(y1), .Q(Count[1]));  // open: Qn, preset, en, reset

  // Other names for the same wires on the sheet: y2_t = Count[0]; y1_t = Count[1]; y0_t = Count[2]
endmodule

module Inputs (
  input  Halt,
  input  CLK,
  output Count_Up,
  output Count_Down,
  output Done_Testing
);

  wire not_1_out;
  wire [5:0] counter_1_q;

  not not_1 (not_1_out, Halt);
  Counter #(.width(6), .max('h21), .ongoal("stay")) counter_1 (
    .count(not_1_out), .Q(counter_1_q), .carry(Done_Testing), .clk(CLK));  // open: load, D, clr
  ROM #(.addrWidth(6), .dataWidth(2)) rom_1 (.addr(counter_1_q), .data({Count_Up, Count_Down}));  // open: sel

  // Notes on the sheet:
  //   contents of rom_1 (hex, n*v repeats v):
  //   0 2 0 2 0 2 0 2 0 2 0 2 0 2 0 2 0 1 0 1 0 1 0 1 0 1 0 1 0 1 0 1
endmodule

module Checker (
  input  Halt_Enable,
  input  Count_Up,
  input  Count_Donw,
  input  [2:0] Your_Answer,
  input  CLK,
  output Correct,
  output [2:0] Solution
);

  wire and_1_out, and_2_out, and_3_out, Gate, nHalt_Enable, or_2_out;

  not not_1 (nHalt_Enable, Halt_Enable);
  and and_1 (and_1_out, Correct, Halt_Enable);
  and and_2 (and_2_out, Count_Up, Gate);
  or or_1 (Gate, nHalt_Enable, and_1_out);
  and and_3 (and_3_out, Gate, Count_Donw);
  or or_2 (or_2_out, and_3_out, and_2_out);
  Counter #(.width(3), .max('h7), .ongoal("stay")) counter_1 (
    .load(and_3_out), .count(or_2_out), .Q(Solution), .clk(CLK));  // open: D, carry, clr
  Comparator #(.width(3)) comparator_1 (.a(Solution), .b(Your_Answer), .eq(Correct));  // open: gt, lt

  // Other names for the same wires on the sheet: Count_Down = Count_Donw
endmodule

module UpDownCounter (
  input  x0,
  input  x1,
  input  x2,
  input  u,
  input  d,
  output y0,
  output y1,
  output y2
);

  wire and_1_out, and_2_out, and_3_out, and_4_out, and_5_out, and_6_out, and_7_out, and_8_out, and_9_out,
       and_10_out, and_11_out, and_12_out, and_13_out, and_14_out, and_15_out, and_16_out, and_17_out,
       not_1_out, not_2_out, not_3_out, not_4_out, not_5_out, not_6_out, not_7_out, not_8_out, not_9_out,
       not_10_out, not_11_out, not_12_out, not_13_out, not_14_out, not_15_out, not_16_out, not_17_out,
       not_18_out, not_19_out, not_20_out;

  not not_1 (not_1_out, d);
  not not_2 (not_2_out, d);
  not not_3 (not_3_out, x1);
  not not_4 (not_4_out, d);
  not not_5 (not_5_out, x2);
  not not_6 (not_6_out, d);
  not not_7 (not_7_out, u);
  not not_8 (not_8_out, x1);
  not not_9 (not_9_out, x2);
  not not_10 (not_10_out, u);
  not not_11 (not_11_out, d);
  not not_12 (not_12_out, x2);
  not not_13 (not_13_out, d);
  not not_14 (not_14_out, u);
  not not_15 (not_15_out, d);
  not not_16 (not_16_out, x2);
  not not_17 (not_17_out, u);
  not not_18 (not_18_out, x2);
  not not_19 (not_19_out, u);
  not not_20 (not_20_out, d);
  and and_1 (and_1_out, x1, x2, u, not_1_out);
  and and_2 (and_2_out, x0, not_2_out);
  and and_3 (and_3_out, x0, u);
  and and_4 (and_4_out, x0, x2);
  and and_5 (and_5_out, x0, x1);
  and and_6 (and_6_out, not_3_out, x2, u, not_4_out);
  and and_7 (and_7_out, x1, not_5_out, not_6_out);
  and and_8 (and_8_out, x1, u, d);
  and and_9 (and_9_out, x1, x2, not_7_out);
  and and_10 (and_10_out, x0, not_8_out, not_9_out, not_10_out, d);
  and and_11 (and_11_out, x0, x1, not_11_out);
  and and_12 (and_12_out, not_12_out, u, not_13_out);
  and and_13 (and_13_out, x2, not_14_out, not_15_out);
  and and_14 (and_14_out, x2, u, d);
  and and_15 (and_15_out, x1, not_16_out, not_17_out, d);
  and and_16 (and_16_out, x0, not_18_out, not_19_out, d);
  and and_17 (and_17_out, x0, x1, x2, not_20_out);
  or or_1 (y0, and_1_out, and_2_out, and_3_out, and_4_out, and_5_out);
  or or_2 (y1, and_6_out, and_7_out, and_8_out, and_9_out, and_10_out, and_11_out);
  or or_3 (y2, and_12_out, and_13_out, and_14_out, and_15_out, and_16_out, and_17_out);
endmodule
